# Fritzing sketch Untitled Sketch (saved by Fritzing 1.0.5)

parts:
  متحكم_ESP32 = Seeed Studio XIAO ESP32S3 Plus [chip_label="XIAO ESP32S3 Plus" package="DIP (Dual Inline)"]
  حساس_التوتر = Grove GSR Sensor
  حساس_نبضات_القلب_ونسبة_الاكسجين_في_الدم = MakerFocus MAX30102
  حساس_حرارة_الجسم = gy-906
  بطارية_ليثيوم = LIPO-110mAh [package=lipo-110]
  مفتاح_تشغيل_/_إيقاف = Pushbutton [package=THT]

nets:
  N1: متحكم_ESP32.D0, حساس_التوتر.SIG
  N2: متحكم_ESP32.D4, حساس_نبضات_القلب_ونسبة_الاكسجين_في_الدم.SDA, حساس_حرارة_الجسم.SDA
  N3: متحكم_ESP32.D5, حساس_نبضات_القلب_ونسبة_الاكسجين_في_الدم.SCL, حساس_حرارة_الجسم.SCL
  GND: متحكم_ESP32.GND, حساس_التوتر.GND, حساس_نبضات_القلب_ونسبة_الاكسجين_في_الدم.GND, حساس_حرارة_الجسم.GND, بطارية_ليثيوم.-
  VIN: متحكم_ESP32.5V, حساس_التوتر.VCC, حساس_نبضات_القلب_ونسبة_الاكسجين_في_الدم.VIN, حساس_حرارة_الجسم.VIN, مفتاح_تشغيل_/_إيقاف.leg1
  N4: بطارية_ليثيوم.+, مفتاح_تشغيل_/_إيقاف.leg0

custom parts:
  Seeed Studio XIAO ESP32S3 Plus: Seeed Studio XIAO ESP32S3 Plus, powered by ESP32-S3's 240MHz Xtensa 32-bit LX7 dual-core processor, brings more SMD pins to the tiny versatile XIAO ESP32S3. While maintaining all the powerful features including WiFi and BLE 5.0 wireless connectivities, 2.4GHz Rod antenna, and ultra-low power consumption of 14μA in deep sleep mode with lithium battery charging management, the Plus variant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
  Grove GSR Sensor: GSR stands for galvanic skin response, is a method of measuring the electrical conductance of the skin. Strong emotion can cause stimulus to your sympathetic nervous system, resulting more sweat being secreted by the sweat glands.
  MakerFocus MAX30102: Oximeter module using the MAX30102 chip. As usual, if you want the mounting holes in pcb, you need to drag a hole over the pad in silkscreen to actually drill the hole (by default they are not drilled)
  gy-906: gy-906 Non-contact PIR I2C interface temperature sensor breakout board.
